# Fritzing sketch skinOS_Zara_v2 (saved by Fritzing 0.9.2b)
breadboards: 1

parts:
  proto1 = Adafruit Feather Wing Proto
  neopixel1 = Neopixel Ring 16
  L1 = Inductor [package="0805 [SMD]"]
  X1 = USB Connectors [package=usb-a-s]
  L2 = Inductor [package="0805 [SMD]"]
  Part1 = Arduino Micro (Rev3)
  R2 = Resistor [tolerance=±5% resistance=330 package="0402 [SMD]"]
  MOTOR1 = Vibration Motor
  MOTOR2 = Vibration Motor
  MOTOR3 = Vibration Motor
  MOTOR4 = Vibration Motor
  R4 = Resistor [tolerance=±5% resistance=1M package="0603 [SMD]"]
  Part2 = PowerBoost 1000 Basic
  Q1 = NPN-Transistor [package="TO92 [THT]"]
  R5 = Resistor [tolerance=±5% resistance=1M package="0603 [SMD]"]
  R6 = Resistor [tolerance=±5% resistance=1M package="0603 [SMD]"]
  R7 = Resistor [tolerance=±5% resistance=1M package="0603 [SMD]"]
  R8 = Resistor [tolerance=±5% resistance=1M package="0603 [SMD]"]
  R9 = Resistor [tolerance=±5% resistance=1M package="0603 [SMD]"]
  U1 = SWITCH_SPDT [package=kps-1290]
  U2 = LIPO-1000mAh [package=lipo-1000]  # not connected
  R10 = Resistor [tolerance=±5% resistance=1k package="0402 [SMD]"]

nets:
  N1: proto1.connector92, Part1.D6_PWM/A7
  N2: neopixel1.IN, R2.Pin_0
  N3: L1.pin_0, Q1.B, U1.O
  N4: L1.pin_1, Part1.D2/SDA
  N5: X1.GND, L2.pin_0
  N6: X1.VBUS, L2.pin_1
  N7: Part1.D3/SCL, R2.Pin_1
  N8: Part1.D5_PWM, R6.Pin_1
  N9: Part1.D9_PWM/A9, R7.Pin_0
  N10: Part1.D10_PWM/A10, Q1.C
  N11: Part1.D11_PWM, R10.Pin_0
  N12: Part1.D12_PWM/A11, R4.Pin_0
  N13: MOTOR1.POS, Part2.5.0V
  N14: MOTOR1.NEG, MOTOR2.POS
  N15: MOTOR2.NEG, MOTOR3.POS
  N16: MOTOR3.NEG, MOTOR4.POS
  N17: MOTOR4.NEG, Q1.E
  N18: R4.Pin_1, R5.Pin_0
  N19: Part2.GND, U1.P
  N20: R5.Pin_1, R6.Pin_0
  N21: R7.Pin_1, R8.Pin_0
  N22: R8.Pin_1, R9.Pin_0

notes:
  NeoPixel Featherwing
  (attaches on Feather Pin D6)
  Adafruit Feather 32u4 Proto
  (use pin #s shown here)
  clarsonic
  induction coil
  w/ circuit
  CHARGIN BASE
  clarsonic
  induction coil
  w/ circuit
  D13
  pin
  Capacitve Touch spots
  850mAh LiPo
  BAT
  pin
  NOTE: coil is not enough to charge battery. Must charge through PowerBoost LiPo charger.
  RST
  pin

custom parts:
  Neopixel Ring 16: Neopixel Ring x16
  Vibration Motor: An eccentric vibration motor!
  PowerBoost 1000 Basic: The PowerBoost 1000 is a little DC/DC boost converter module that can run from 1.8V batteries or higher, and convert the battery output to 5.2V DC for running your 5V projects. At its heart is a TPS61030 boost converter from TI. This boost converter chip has some really nice extras such as low battery detection, 4A internal switch, synchronous conversion, excellent efficiency, and 700KHz high-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
